// Logisim project RISC-V.circ as structural Verilog: 20 circuits, main circuit main
module main (
  input  CLK,
  output [4:0] out_2,
  output [1:0] out_3,
  output [2:0] out_4,
  output out_5,
  output [1:0] out_6,
  output [1:0] out_7,
  output out_8,
  output out_9,
  output out_10,
  output [1:0] out_11,
  output out_12
);

  wire CLK_t, CLR_regs, csr_1_invalid_address, csr_1_invalid_read, csr_1_invalid_write, csr_1_stop_clock,
       i_o_1_clk_2, i_o_1_clk_3, i_o_1_clr_2, i_o_1_clr_3, i_o_1_enable_keyboard, i_o_1_enable_tty,
       i_o_1_valid_adress, keyboard_1_avail, memory_1_out_of_range_exception,
       memory_1_word_aligned_exception, memory_1_write_align_exception,
       pc_1_instruction_adress_misaligned_exception, Start_out, Stop_out;
  wire [2:0] compare_1_flags, split_instruction_1_func3;
  wire [4:0] split_instruction_1_rd, split_instruction_1_rs1, split_instruction_1_rs2;
  wire [6:0] i_o_1_tty_data, keyboard_1_data, split_instruction_1_func7, split_instruction_1_opcode;
  wire [11:0] split_instruction_1_csr_specifier;
  wire [31:0] add_4_1_output, alu_1_result, csr_1_output, i_o_1_data_out, i_o_1_screen_1, i_o_1_screen_2,
       i_o_1_screen_3, i_o_1_screen_4, i_o_1_screen_5, i_o_1_screen_6, i_o_1_screen_7, i_o_1_screen_8,
       i_o_1_screen_9, i_o_1_screen_10, i_o_1_screen_11, i_o_1_screen_12, i_o_1_screen_13, i_o_1_screen_14,
       i_o_1_screen_15, i_o_1_screen_16, i_o_1_screen_17, i_o_1_screen_18, i_o_1_screen_19, i_o_1_screen_20,
       i_o_1_screen_21, i_o_1_screen_22, i_o_1_screen_23, i_o_1_screen_24, i_o_1_screen_25, i_o_1_screen_26,
       i_o_1_screen_27, i_o_1_screen_28, i_o_1_screen_29, i_o_1_screen_30, i_o_1_screen_31, i_o_1_screen_32,
       memory_1_data, memory_1_instruction, multiplexer_1_out, multiplexer_2_out, multiplexer_3_out, pc_1_pc,
       register_file_1_read_data_1, register_file_1_read_data_2, split_instruction_1_imm_b,
       split_instruction_1_imm_i, split_instruction_1_imm_j, split_instruction_1_imm_s,
       split_instruction_1_imm_u;

  LED led_1 (.in(pc_1_instruction_adress_misaligned_exception));
  PC pc_1 (
    .Jump_Addr(alu_1_result), .PC(pc_1_pc), .Jump(out_10), .CLK(CLK_t), .RST(CLR_regs),
    .Instruction_adress_misaligned_exception(pc_1_instruction_adress_misaligned_exception));
  LED led_2 (.in(memory_1_write_align_exception));
  Keyboard #(.buflen(256), .trigger("falling")) keyboard_1 (
    .clk(i_o_1_clk_2), .re(i_o_1_clr_2), .clr(i_o_1_enable_keyboard), .avail(keyboard_1_avail),
    .data(keyboard_1_data));
  I_O i_o_1 (
    .CLK_2(i_o_1_clk_2), .CLR_2(i_o_1_clr_2), .Enable_Keyboard(i_o_1_enable_keyboard),
    .Keyboard_Available(keyboard_1_avail), .Keyboard_Data(keyboard_1_data), .CLK_3(i_o_1_clk_3),
    .Enable_TTY(i_o_1_enable_tty), .CLR_3(i_o_1_clr_3), .TTY_Data(i_o_1_tty_data), .Screen_1(i_o_1_screen_1),
    .Screen_2(i_o_1_screen_2), .Screen_3(i_o_1_screen_3), .Screen_4(i_o_1_screen_4),
    .Screen_5(i_o_1_screen_5), .Screen_6(i_o_1_screen_6), .Screen_7(i_o_1_screen_7),
    .Screen_8(i_o_1_screen_8), .Screen_9(i_o_1_screen_9), .Screen_10(i_o_1_screen_10),
    .Screen_11(i_o_1_screen_11), .Screen_12(i_o_1_screen_12), .Screen_13(i_o_1_screen_13),
    .Screen_14(i_o_1_screen_14), .Screen_15(i_o_1_screen_15), .Screen_16(i_o_1_screen_16),
    .Screen_17(i_o_1_screen_17), .Screen_18(i_o_1_screen_18), .Screen_19(i_o_1_screen_19),
    .Screen_20(i_o_1_screen_20), .Screen_21(i_o_1_screen_21), .Screen_22(i_o_1_screen_22),
    .Screen_23(i_o_1_screen_23), .Screen_24(i_o_1_screen_24), .Screen_25(i_o_1_screen_25),
    .Screen_26(i_o_1_screen_26), .Screen_27(i_o_1_screen_27), .Screen_28(i_o_1_screen_28),
    .Screen_29(i_o_1_screen_29), .Screen_30(i_o_1_screen_30), .Screen_31(i_o_1_screen_31),
    .Screen_32(i_o_1_screen_32), .Data_in(register_file_1_read_data_2), .Address(alu_1_result),
    .Valid_Adress(i_o_1_valid_adress), .CLK(CLK_t), .CLR(CLR_regs), .Write(out_8), .Data_out(i_o_1_data_out));
  LED led_3 (.in(memory_1_word_aligned_exception));
  LED led_4 (.in(memory_1_out_of_range_exception));
  Memory memory_1 (
    .Write_Data(register_file_1_read_data_2), .PC(pc_1_pc), .Data_addr(alu_1_result), .Data(memory_1_data),
    .Instruction(memory_1_instruction), .Write_align_exception(memory_1_write_align_exception),
    .Word_aligned_exception(memory_1_word_aligned_exception),
    .Out_of_range_exception(memory_1_out_of_range_exception), .I_O_Data(i_o_1_data_out),
    .I_O_In_Range(i_o_1_valid_adress), .CLK(CLK_t), .Write(out_8), .Data_Src(out_7),
    .Signed__Unsigned(out_5), .Data_size(out_6), .CLR_regs(CLR_regs));
  TTY #(.rows(16), .cols(40), .trigger("falling")) tty_1 (
    .data(i_o_1_tty_data), .clk(i_o_1_clk_3), .we(i_o_1_enable_tty), .clr(i_o_1_clr_3));
  Split_instruction split_instruction_1 (
    .Instruction(memory_1_instruction), .Opcode(split_instruction_1_opcode),
    .Func3(split_instruction_1_func3), .Func7(split_instruction_1_func7), .Rd(split_instruction_1_rd),
    .Rs1(split_instruction_1_rs1), .Rs2(split_instruction_1_rs2), .Imm_I(split_instruction_1_imm_i),
    .Imm_S(split_instruction_1_imm_s), .Imm_B(split_instruction_1_imm_b), .Imm_U(split_instruction_1_imm_u),
    .Imm_J(split_instruction_1_imm_j), .CSR_Specifier(split_instruction_1_csr_specifier));
  Control control_1 (
    .Opcode(split_instruction_1_opcode), .Func3(split_instruction_1_func3),
    .Func7(split_instruction_1_func7), .ALU_op(out_2), .ALU_Src1(out_3), .DataSrc(out_7), .RegWrite(out_9),
    .Jump(out_10), .ALU_Src2(out_4), .Flags(compare_1_flags), .RAMWrite(out_8), .DataSize(out_6),
    .DataSign(out_5), .CSR_Op(out_11), .CSR_Imm(out_12));
  LED led_5 (.in(csr_1_invalid_read));
  Add_4 add_4_1 (.Input(pc_1_pc), .Output(add_4_1_output));
  LED led_6 (.in(csr_1_invalid_write));
  LED led_7 (.in(csr_1_invalid_address));
  CSR csr_1 (
    .Rs1_uimm(split_instruction_1_rs1), .Rd(split_instruction_1_rd),
    .CSR_specifier(split_instruction_1_csr_specifier), .Output(csr_1_output),
    .Rs1Val(register_file_1_read_data_1), .Invalid_Read(csr_1_invalid_read),
    .Invalid_Write(csr_1_invalid_write), .Invalid_Address(csr_1_invalid_address),
    .Operation____RW_RS_RC(out_11), .DataSrc(out_7), .CLK(CLK_t), .CLR(CLR_regs), .Imm(out_12),
    .Stop_clock(csr_1_stop_clock));
  Multiplexer #(.select(2), .width(32), .enable("false")) multiplexer_1 (
    .in0(memory_1_data), .in1(alu_1_result), .in2(add_4_1_output), .in3(csr_1_output),
    .out(multiplexer_1_out), .sel(out_7));
  DotMatrix #(.inputtype("row"), .matrixcols(32), .matrixrows(32)) dotmatrix_1 (
    .row0(i_o_1_screen_1), .row1(i_o_1_screen_2), .row2(i_o_1_screen_3), .row3(i_o_1_screen_4),
    .row4(i_o_1_screen_5), .row5(i_o_1_screen_6), .row6(i_o_1_screen_7), .row7(i_o_1_screen_8),
    .row8(i_o_1_screen_9), .row9(i_o_1_screen_10), .row10(i_o_1_screen_11), .row11(i_o_1_screen_12),
    .row12(i_o_1_screen_13), .row13(i_o_1_screen_14), .row14(i_o_1_screen_15), .row15(i_o_1_screen_16),
    .row16(i_o_1_screen_17), .row17(i_o_1_screen_18), .row18(i_o_1_screen_19), .row19(i_o_1_screen_20),
    .row20(i_o_1_screen_21), .row21(i_o_1_screen_22), .row22(i_o_1_screen_23), .row23(i_o_1_screen_24),
    .row24(i_o_1_screen_25), .row25(i_o_1_screen_26), .row26(i_o_1_screen_27), .row27(i_o_1_screen_28),
    .row28(i_o_1_screen_29), .row29(i_o_1_screen_30), .row30(i_o_1_screen_31), .row31(i_o_1_screen_32));
  Compare compare_1 (.Flags(compare_1_flags), .Rs1(register_file_1_read_data_1), .Rs2(register_file_1_read_data_2));
  Register_File register_file_1 (
    .Read_Data_1(register_file_1_read_data_1), .Read_Data_2(register_file_1_read_data_2),
    .Read_Reg_1(split_instruction_1_rs1), .Read_Reg_2(split_instruction_1_rs2),
    .Write_Reg(split_instruction_1_rd), .Write_data(multiplexer_1_out), .RegWrite(out_9), .CLK(CLK_t),
    .CLR(CLR_regs));
  CLK clk_1 (
    .Stop_clock(csr_1_stop_clock), .CLK(CLK_t), .CLR(CLR_regs), .Start(Start_out), .Manual(CLK),
    .Stop(Stop_out));
  Button Stop (.out(Stop_out));
  Button Reset (.out(CLR_regs));
  Button Start (.out(Start_out));
  Multiplexer #(.select(2), .width(32), .enable("false")) multiplexer_2 (
    .in0(register_file_1_read_data_1), .in1(split_instruction_1_imm_u), .in2(split_instruction_1_imm_j),
    .in3(split_instruction_1_imm_b), .out(multiplexer_2_out), .sel(out_3));
  Multiplexer #(.select(3), .width(32), .enable("false")) multiplexer_3 (
    .in0({32{1'b0}}), .in1(register_file_1_read_data_2), .in2(split_instruction_1_imm_i), .in3(pc_1_pc),
    .in4(split_instruction_1_imm_s), .out(multiplexer_3_out), .sel(out_4));  // open: in5, in6, in7
  ALU alu_1 (.Operand1(multiplexer_2_out), .Operand2(multiplexer_3_out), .Operation(out_2), .Result(alu_1_result));

  // Other names for the same wires on the sheet: ALU_op[4:0] = out_2; ALU_Src1[1:0] = out_3; ALU_Src2[2:0] = out_4;
  //   CSR_Imm = out_12; CSR_Op[1:0] = out_11; Data_Sign = out_5; Data_Size[1:0] = out_6; Data_Src[1:0] = out_7;
  //   Jump = out_10; RAMWrite = out_8; RegWrite = out_9

  // Notes on the sheet:
  //   Data-Src: RAM, ALU, PC, CSR
  //   ALU-Src1: Reg, Imm-U, Imm-J, Imm-B
  //   ALU-Src2: Zero, Reg, Imm-I, PC, Imm-S
endmodule

module RAM (
  input  [31:0] Write_Data,
  input  [31:0] PC,
  input  [31:0] Data_addr,
  input  CLK,
  input  Write,
  input  [1:0] Data_Src,
  input  Signed__Unsigned,
  input  [1:0] Data_size,
  input  CLR_regs,
  output Write_align_exception,
  output Word_aligned_exception,
  output Out_of_range_exception,
  output [31:0] Data,
  output [31:0] Instruction
);

  wire and_4_out, not_1_out, or_1_out, replace_part_1_misaligned_replace, split_word_1_misaligned_split;
  wire [31:0] multiplexer_1_out, ram_1_data, replace_part_1_output;

  and and_1 (Write_align_exception, replace_part_1_misaligned_replace, Write);
  Multiplexer #(.width(32), .enable("false")) multiplexer_1 (
    .in0(PC), .in1(Data_addr), .out(multiplexer_1_out), .sel(CLK));
  and and_2 (Word_aligned_exception, split_word_1_misaligned_split, and_4_out);
  Replace_part replace_part_1 (
    .Replacement(Write_Data), .Address(multiplexer_1_out[1:0]), .Size__Byte_Half_Word(Data_size),
    .Misaligned_Replace(replace_part_1_misaligned_replace), .Output(replace_part_1_output), .Input(ram_1_data));
  or or_1 (or_1_out, multiplexer_1_out[31], multiplexer_1_out[30], multiplexer_1_out[29], multiplexer_1_out[28], multiplexer_1_out[27], multiplexer_1_out[26]);
  and and_3 (Out_of_range_exception, or_1_out, and_4_out);
  RAM_part #(.addrWidth(24), .dataWidth(32), .bus("separate")) ram_1 (
    .addr(multiplexer_1_out[25:2]), .din(replace_part_1_output), .data(ram_1_data), .str(Write),
    .clk(not_1_out));  // open: sel, ld, clr
  not not_1 (not_1_out, CLK);
  and and_4 (and_4_out, CLK, ~Data_Src[1], ~Data_Src[0]);  // AND_Gate
  Split_word split_word_1 (
    .Address(multiplexer_1_out[1:0]), .Size__Byte_Half_Word(Data_size), .Signed__Unsigned(Signed__Unsigned),
    .Misaligned_split(split_word_1_misaligned_split), .Output(Data), .Input(ram_1_data));
  Register #(.width(32)) register_1 (.D(ram_1_data), .Q(Instruction), .clk(CLK), .clr(CLR_regs));  // open: en

  // Notes on the sheet:
  //   For now only 26 bit adresses are allowed
  //   First 6 bits, should be 0 otherwise adress not in range
  //   Allow Exception
endmodule

module Register_File (
  input  [4:0] Read_Reg_1,
  input  [4:0] Read_Reg_2,
  input  [4:0] Write_Reg,
  input  [31:0] Write_data,
  input  RegWrite,
  input  CLK,
  input  CLR,
  output [31:0] Read_Data_1,
  output [31:0] Read_Data_2
);

  wire decoder_1_out0, decoder_1_out1, decoder_1_out2, decoder_1_out3, decoder_1_out4, decoder_1_out5,
       decoder_1_out6, decoder_1_out7, decoder_1_out8, decoder_1_out9, decoder_1_out10, decoder_1_out11,
       decoder_1_out12, decoder_1_out13, decoder_1_out14, decoder_1_out15, decoder_1_out16, decoder_1_out17,
       decoder_1_out18, decoder_1_out19, decoder_1_out20, decoder_1_out21, decoder_1_out22, decoder_1_out23,
       decoder_1_out24, decoder_1_out25, decoder_1_out26, decoder_1_out27, decoder_1_out28, decoder_1_out29,
       decoder_1_out30, decoder_1_out31;
  wire [31:0] register_1_q, register_2_q, register_3_q, register_4_q, register_5_q, register_6_q,
       register_7_q, register_8_q, register_9_q, register_10_q, register_11_q, register_12_q, register_13_q,
       register_14_q, register_15_q, register_16_q, register_17_q, register_18_q, register_19_q,
       register_20_q, register_21_q, register_22_q, register_23_q, register_24_q, register_25_q,
       register_26_q, register_27_q, register_28_q, register_29_q, register_30_q, register_31_q;

  Decoder #(.select(5), .disabled(0)) decoder_1 (
    .out0(decoder_1_out0), .out1(decoder_1_out1), .out2(decoder_1_out2), .out3(decoder_1_out3),
    .out4(decoder_1_out4), .out5(decoder_1_out5), .out6(decoder_1_out6), .out7(decoder_1_out7),
    .out8(decoder_1_out8), .out9(decoder_1_out9), .out10(decoder_1_out10), .out11(decoder_1_out11),
    .out12(decoder_1_out12), .out13(decoder_1_out13), .out14(decoder_1_out14), .out15(decoder_1_out15),
    .out16(decoder_1_out16), .out17(decoder_1_out17), .out18(decoder_1_out18), .out19(decoder_1_out19),
    .out20(decoder_1_out20), .out21(decoder_1_out21), .out22(decoder_1_out22), .out23(decoder_1_out23),
    .out24(decoder_1_out24), .out25(decoder_1_out25), .out26(decoder_1_out26), .out27(decoder_1_out27),
    .out28(decoder_1_out28), .out29(decoder_1_out29), .out30(decoder_1_out30), .out31(decoder_1_out31),
    .sel(Write_Reg), .en(RegWrite));
  Register #(.width(32), .trigger("falling")) register_1 (
    .D(Write_data), .en(decoder_1_out1), .Q(register_1_q), .clk(CLK), .clr(CLR));
  Register #(.width(32), .trigger("falling")) register_2 (
    .D(Write_data), .en(decoder_1_out2), .Q(register_2_q), .clk(CLK), .clr(CLR));
  Register #(.width(32), .trigger("falling")) register_3 (
    .D(Write_data), .en(decoder_1_out3), .Q(register_3_q), .clk(CLK), .clr(CLR));
  Register #(.width(32), .trigger("falling")) register_4 (
    .D(Write_data), .en(decoder_1_out4), .Q(register_4_q), .clk(CLK), .clr(CLR));
  Register #(.width(32), .trigger("falling")) register_5 (
    .D(Write_data), .en(decoder_1_out5), .Q(register_5_q), .clk(CLK), .clr(CLR));
  Register #(.width(32), .trigger("falling")) register_6 (
    .D(Write_data), .en(decoder_1_out6), .Q(register_6_q), .clk(CLK), .clr(CLR));
  Register #(.width(32), .trigger("falling")) register_7 (
    .D(Write_data), .en(decoder_1_out7), .Q(register_7_q), .clk(CLK), .clr(CLR));
  Register #(.width(32), .trigger("falling")) register_8 (
    .D(Write_data), .en(decoder_1_out8), .Q(register_8_q), .clk(CLK), .clr(CLR));
  Register #(.width(32), .trigger("falling")) register_9 (
    .D(Write_data), .en(decoder_1_out9), .Q(register_9_q), .clk(CLK), .clr(CLR));
  Register #(.width(32), .trigger("falling")) register_10 (
    .D(Write_data), .en(decoder_1_out10), .Q(register_10_q), .clk(CLK), .clr(CLR));
  Register #(.width(32), .trigger("falling")) register_11 (
    .D(Write_data), .en(decoder_1_out11), .Q(register_11_q), .clk(CLK), .clr(CLR));
  Register #(.width(32), .trigger("falling")) register_12 (
    .D(Write_data), .en(decoder_1_out12), .Q(register_12_q), .clk(CLK), .clr(CLR));
  Register #(.width(32), .trigger("falling")) register_13 (
    .D(Write_data), .en(decoder_1_out13), .Q(register_13_q), .clk(CLK), .clr(CLR));
  Register #(.width(32), .trigger("falling")) register_14 (
    .D(Write_data), .en(decoder_1_out14), .Q(register_14_q), .clk(CLK), .clr(CLR));
  Register #(.width(32), .trigger("falling")) register_15 (
    .D(Write_data), .en(decoder_1_out15), .Q(register_15_q), .clk(CLK), .clr(CLR));
  Register #(.width(32), .trigger("falling")) register_16 (
    .D(Write_data), .en(decoder_1_out16), .Q(register_16_q), .clk(CLK), .clr(CLR));
  Register #(.width(32), .trigger("falling")) register_17 (
    .D(Write_data), .en(decoder_1_out17), .Q(register_17_q), .clk(CLK), .clr(CLR));
  Register #(.width(32), .trigger("falling")) register_18 (
    .D(Write_data), .en(decoder_1_out18), .Q(register_18_q), .clk(CLK), .clr(CLR));
  Register #(.width(32), .trigger("falling")) register_19 (
    .D(Write_data), .en(decoder_1_out19), .Q(register_19_q), .clk(CLK), .clr(CLR));
  Register #(.width(32), .trigger("falling")) register_20 (
    .D(Write_data), .en(decoder_1_out20), .Q(register_20_q), .clk(CLK), .clr(CLR));
  Register #(.width(32), .trigger("falling")) register_21 (
    .D(Write_data), .en(decoder_1_out21), .Q(register_21_q), .clk(CLK), .clr(CLR));
  Register #(.width(32), .trigger("falling")) register_22 (
    .D(Write_data), .en(decoder_1_out22), .Q(register_22_q), .clk(CLK), .clr(CLR));
  Register #(.width(32), .trigger("falling")) register_23 (
    .D(Write_data), .en(decoder_1_out23), .Q(register_23_q), .clk(CLK), .clr(CLR));
  Register #(.width(32), .trigger("falling")) register_24 (
    .D(Write_data), .en(decoder_1_out24), .Q(register_24_q), .clk(CLK), .clr(CLR));
  Register #(.width(32), .trigger("falling")) register_25 (
    .D(Write_data), .en(decoder_1_out25), .Q(register_25_q), .clk(CLK), .clr(CLR));
  Register #(.width(32), .trigger("falling")) register_26 (
    .D(Write_data), .en(decoder_1_out26), .Q(register_26_q), .clk(CLK), .clr(CLR));
  Register #(.width(32), .trigger("falling")) register_27 (
    .D(Write_data), .en(decoder_1_out27), .Q(register_27_q), .clk(CLK), .clr(CLR));
  Register #(.width(32), .trigger("falling")) register_28 (
    .D(Write_data), .en(decoder_1_out28), .Q(register_28_q), .clk(CLK), .clr(CLR));
  Register #(.width(32), .trigger("falling")) register_29 (
    .D(Write_data), .en(decoder_1_out29), .Q(register_29_q), .clk(CLK), .clr(CLR));
  Register #(.width(32), .trigger("falling")) register_30 (
    .D(Write_data), .en(decoder_1_out30), .Q(register_30_q), .clk(CLK), .clr(CLR));
  Register #(.width(32), .trigger("falling")) register_31 (
    .D(Write_data), .en(decoder_1_out31), .Q(register_31_q), .clk(CLK), .clr(CLR));
  Multiplexer #(.select(5), .width(32), .enable("false")) multiplexer_1 (
    .in0({32{1'b0}}), .in1(register_1_q), .in2(register_2_q), .in3(register_3_q), .in4(register_4_q),
    .in5(register_5_q), .in6(register_6_q), .in7(register_7_q), .in8(register_8_q), .in9(register_9_q),
    .in10(register_10_q), .in11(register_11_q), .in12(register_12_q), .in13(register_13_q),
    .in14(register_14_q), .in15(register_15_q), .in16(register_16_q), .in17(register_17_q),
    .in18(register_18_q), .in19(register_19_q), .in20(register_20_q), .in21(register_21_q),
    .in22(register_22_q), .in23(register_23_q), .in24(register_24_q), .in25(register_25_q),
    .in26(register_26_q), .in27(register_27_q), .in28(register_28_q), .in29(register_29_q),
    .in30(register_30_q), .in31(register_31_q), .out(Read_Data_1), .sel(Read_Reg_1));
  Multiplexer #(.select(5), .width(32), .enable("false")) multiplexer_2 (
    .in0({32{1'b0}}), .in1(register_1_q), .in2(register_2_q), .in3(register_3_q), .in4(register_4_q),
    .in5(register_5_q), .in6(register_6_q), .in7(register_7_q), .in8(register_8_q), .in9(register_9_q),
    .in10(register_10_q), .in11(register_11_q), .in12(register_12_q), .in13(register_13_q),
    .in14(register_14_q), .in15(register_15_q), .in16(register_16_q), .in17(register_17_q),
    .in18(register_18_q), .in19(register_19_q), .in20(register_20_q), .in21(register_21_q),
    .in22(register_22_q), .in23(register_23_q), .in24(register_24_q), .in25(register_25_q),
    .in26(register_26_q), .in27(register_27_q), .in28(register_28_q), .in29(register_29_q),
    .in30(register_30_q), .in31(register_31_q), .out(Read_Data_2), .sel(Read_Reg_2));
endmodule

module PC (
  input  [31:0] Jump_Addr,
  input  Jump,
  input  CLK,
  input  RST,
  output Instruction_adress_misaligned_exception,
  output [31:0] PC
);

  wire buffer_1_out, buffer_2_out, buffer_3_out, nor_1_out, not_1_out, not_2_out, or_1_out, or_2_out;
  wire [31:0] multiplexer_1_out;

  Multiplexer #(.width(32), .enable("false")) multiplexer_1 (
    .in0(Jump_Addr), .in1(32'h400000), .out(multiplexer_1_out), .sel(buffer_1_out));
  or or_1 (or_1_out, Jump, buffer_1_out);
  buf buffer_1 (buffer_1_out, buffer_2_out);
  buf buffer_2 (buffer_2_out, buffer_3_out);
  buf buffer_3 (buffer_3_out, RST);
  and and_1 (Instruction_adress_misaligned_exception, or_1_out, multiplexer_1_out[1]);
  Counter #(.width(30), .max('h3fffffff), .trigger("falling")) counter_1 (
    .load(or_1_out), .D(multiplexer_1_out[31:2]), .count(not_1_out), .Q(PC[31:2]), .clk(or_2_out));  // open: carry, clr
  not not_1 (not_1_out, or_1_out);
  or or_2 (or_2_out, CLK, nor_1_out);
  nor nor_1 (nor_1_out, not_2_out, RST);
  not not_2 (not_2_out, RST);

  assign PC[1:0] = 2'b00;

  // Notes on the sheet:
  //   Last two bits must always be 0, so discard them everywhere
  //   Start Address
endmodule

module Split_instruction (
  input  [31:0] Instruction,
  output [6:0] Opcode,
  output [2:0] Func3,
  output [6:0] Func7,
  output [4:0] Rd,
  output [4:0] Rs1,
  output [4:0] Rs2,
  output [31:0] Imm_I,
  output [31:0] Imm_S,
  output [31:0] Imm_B,
  output [31:0] Imm_U,
  output [31:0] Imm_J,
  output [11:0] CSR_Specifier
);

  assign Imm_I = {{20{Instruction[31]}}, Instruction[31:20]};  // Bit_Extender bit_extender_1
  assign Imm_S = {{20{Instruction[31]}}, {Instruction[31:25], Instruction[11:7]}};  // Bit_Extender bit_extender_2
  assign Imm_B = {{19{Instruction[31]}}, {Instruction[31], Instruction[7], Instruction[30:25], Instruction[11:8], 1'b0}};  // Bit_Extender bit_extender_3
  assign Imm_J = {{11{Instruction[31]}}, {Instruction[31], Instruction[19:12], Instruction[20], Instruction[30:21], 1'b0}};  // Bit_Extender bit_extender_4

  assign CSR_Specifier = Instruction[31:20];
  assign Func3 = Instruction[14:12];
  assign Func7 = Instruction[31:25];
  assign Imm_U = {Instruction[31:12], {12{1'b0}}};
  assign Opcode = Instruction[6:0];
  assign Rd = Instruction[11:7];
  assign Rs1 = Instruction[19:15];
  assign Rs2 = Instruction[24:20];
endmodule

module ALU (
  input  [31:0] Operand1,
  input  [31:0] Operand2,
  input  [4:0] Operation,
  output [31:0] Result
);

  wire and_2_out, and_3_out, button_1_out, clock_1_out, comparator_1_lt, comparator_2_lt, comparator_3_eq,
       d_ff_1_q, not_1_out, not_2_out, or_2_out, xor_2_out;
  wire [0:0] adder_2_cout;
  wire [1:0] adder_2_out, adder_3_out, multiplier_2_cout, multiplier_2_out, multiplier_3_cout,
       multiplier_3_out, multiplier_5_cout, multiplier_5_out, multiplier_6_cout, multiplier_6_out;
  wire [3:0] multiplier_4_cout, multiplier_4_out;
  wire [7:0] counter_1_q;
  wire [31:0] adder_1_out, and_1_out, bit_extender_1_out, bit_extender_2_out, divider_1_out, divider_1_rem,
       multiplier_1_cout, multiplier_1_out, negate_1_out_3, negate_2_out_3, negate_3_out_3, negate_4_out_3,
       or_1_out, shifter_1_out, shifter_2_out, shifter_3_out, subtractor_1_out, xor_1_out;

  Adder #(.width(32)) adder_1 (.a(Operand1), .b(Operand2), .out(adder_1_out));  // open: cin, cout
  Subtractor #(.width(32)) subtractor_1 (.a(Operand1), .b(Operand2), .out(subtractor_1_out));  // open: bin, bout
  assign xor_1_out = Operand1 ^ Operand2;  // XOR_Gate xor_1, 32 bits wide
  assign or_1_out = Operand1 | Operand2;  // OR_Gate or_1, 32 bits wide
  assign and_1_out = Operand1 & Operand2;  // AND_Gate and_1, 32 bits wide
  Shifter #(.width(32)) shifter_1 (.in(Operand1), .\dist (Operand2[4:0]), .out(shifter_1_out));
  Shifter #(.width(32), .shift("lr")) shifter_2 (.in(Operand1), .\dist (Operand2[4:0]), .out(shifter_2_out));
  Shifter #(.width(32), .shift("ar")) shifter_3 (.in(Operand1), .\dist (Operand2[4:0]), .out(shifter_3_out));
  Comparator #(.width(32)) comparator_1 (.a(Operand1), .b(Operand2), .lt(comparator_1_lt));  // open: gt, eq
  Comparator #(.width(32), .mode("unsigned")) comparator_2 (
    .a(Operand1), .b(Operand2), .lt(comparator_2_lt));  // open: gt, eq
  Multiplier #(.width(32)) multiplier_1 (
    .a(Operand1), .b(Operand2), .out(multiplier_1_out), .cout(multiplier_1_cout));  // open: cin
  not not_1 (not_1_out, Operation[0]);
  assign bit_extender_1_out = {{31{1'b0}}, comparator_1_lt};  // Bit_Extender bit_extender_1
  assign bit_extender_2_out = {{31{1'b0}}, comparator_2_lt};  // Bit_Extender bit_extender_2
  and and_2 (and_2_out, not_1_out, Operand1[31]);
  Negate negate_1 (.Invert(and_2_out), .out_3(negate_1_out_3), .in_2(Operand1));
  and and_3 (and_3_out, not_1_out, Operand2[31]);
  Negate negate_2 (.Invert(and_3_out), .out_3(negate_2_out_3), .in_2(Operand2));
  xor xor_2 (xor_2_out, and_2_out, and_3_out);
  Divider #(.width(32)) divider_1 (
    .a(negate_1_out_3), .b(negate_2_out_3), .out(divider_1_out), .rem(divider_1_rem));  // open: upper
  Negate negate_3 (.Invert(xor_2_out), .out_3(negate_3_out_3), .in_2(divider_1_out));
  Negate negate_4 (.Invert(and_2_out), .out_3(negate_4_out_3), .in_2(divider_1_rem));
  Counter counter_1 (.Q(counter_1_q), .clk(clock_1_out));  // open: load, D, count, carry, clr
  Multiplier #(.width(2)) multiplier_2 (
    .a(counter_1_q[1:0]), .b(counter_1_q[5:4]), .out(multiplier_2_out), .cout(multiplier_2_cout));  // open: cin
  Multiplier #(.width(2)) multiplier_3 (
    .a(counter_1_q[1:0]), .b(counter_1_q[7:6]), .out(multiplier_3_out), .cin(multiplier_2_cout),
    .cout(multiplier_3_cout));
  Multiplier #(.width(4)) multiplier_4 (
    .a(counter_1_q[7:4]), .b(counter_1_q[3:0]), .out(multiplier_4_out), .cout(multiplier_4_cout));  // open: cin
  Clock clock_1 (.out(clock_1_out));
  Multiplier #(.width(2)) multiplier_5 (
    .a(counter_1_q[3:2]), .b(counter_1_q[5:4]), .out(multiplier_5_out), .cin(multiplier_3_out),
    .cout(multiplier_5_cout));
  Adder #(.width(2)) adder_2 (
    .a(multiplier_5_cout), .b(multiplier_3_cout), .out(adder_2_out), .cout(adder_2_cout[0]));  // open: cin
  Multiplier #(.width(2)) multiplier_6 (
    .a(counter_1_q[3:2]), .b(counter_1_q[7:6]), .out(multiplier_6_out), .cin(adder_2_out),
    .cout(multiplier_6_cout));
  // Probe on {multiplier_4_cout, multiplier_4_out}
  Multiplexer #(.select(5), .width(32), .enable("false")) multiplexer_1 (
    .in0(adder_1_out), .in1(subtractor_1_out), .in2(xor_1_out), .in3(or_1_out), .in4(and_1_out),
    .in5(shifter_1_out), .in6(shifter_2_out), .in7(shifter_3_out), .in10(bit_extender_1_out),
    .in11(bit_extender_2_out), .in16(multiplier_1_out), .in17(multiplier_1_cout), .in20(negate_3_out_3),
    .in21(negate_3_out_3), .in22(negate_4_out_3), .in23(negate_4_out_3), .out(Result), .sel(Operation));  // open: in8, in9, in12, in13, in14, in15, in18, in19, in24, in25, in26, in27, in28, in29, in30, in31
  // Probe on {adder_3_out, multiplier_6_out, multiplier_5_out, multiplier_2_out}
  Adder #(.width(2)) adder_3 (
    .a({1'b0, adder_2_cout[0]}), .b(multiplier_6_cout), .out(adder_3_out));  // open: cin, cout
  Comparator comparator_3 (
    .a({adder_3_out, multiplier_6_out, multiplier_5_out, multiplier_2_out}),
    .b({multiplier_4_cout, multiplier_4_out}), .eq(comparator_3_eq));  // open: gt, lt
  not not_2 (not_2_out, comparator_3_eq);
  D_Flip_Flop d_ff_1 (.clk(clock_1_out), .D(or_2_out), .Q(d_ff_1_q), .reset(button_1_out));  // open: Qn, preset, en
  or or_2 (or_2_out, d_ff_1_q, not_2_out);
  Button button_1 (.out(button_1_out));

  // Notes on the sheet:
  //   32 bit multiply works incorrectly, it is signed while smaller ones are unsigned. This means unsiged and signed-unsigned multipliers still need to be implemented
  //   Signed and unsigned division are implemented using the same circuit, and one of the bits of the operation is used to choose
  //   Unsigned multiply circuit, unsigned-signed not worked out yet
  //   Test circuit
endmodule

module Negate (
  input  Invert,
  input  [31:0] in_2,
  output [31:0] out_3
);

  wire [31:0] subtractor_1_out;

  Multiplexer #(.width(32), .enable("false")) multiplexer_1 (
    .in0(in_2), .in1(subtractor_1_out), .out(out_3), .sel(Invert));
  Subtractor #(.width(32)) subtractor_1 (.a({32{1'b0}}), .b(in_2), .out(subtractor_1_out));  // open: bin, bout
endmodule

module Control (
  input  [6:0] Opcode,
  input  [2:0] Func3,
  input  [6:0] Func7,
  input  [2:0] Flags,
  output [4:0] ALU_op,
  output [1:0] ALU_Src1,
  output [2:0] ALU_Src2,
  output DataSign,
  output [1:0] DataSize,
  output [1:0] DataSrc,
  output RAMWrite,
  output RegWrite,
  output Jump,
  output [1:0] CSR_Op,
  output CSR_Imm
);

  ROM #(.addrWidth(20), .dataWidth(21)) rom_1 (
    .addr({Flags, Opcode, Func3, Func7}),
    .data({CSR_Imm, CSR_Op, Jump, RegWrite, RAMWrite, DataSrc, DataSize, DataSign, ALU_Src2, ALU_Src1, ALU_op}));  // open: sel

  // Notes on the sheet:
  //   contents of rom_1 (hex, n*v repeats v):
  //   3072*43000 128*50100 128*50900 128*51100 128*43000 128*50500 128*50d00 15616*43000 128*53100 53105
  //   127*53100 128*5310a 128*5310b 128*53102 53106 31*53100 53107 95*53100 128*53103 128*53104 3072*43000
  //   1024*531a0 11264*43000 128*4a200 128*4aa00 128*4b200 16000*43000 53080 53090 30*53080 53081 95*53080
  //   53085 53093 126*53080 5308a 53091 126*53080 5308b 53092 126*53080 53082 53094 126*53080 53086 53095
  //   30*53080 53087 95*53080 53083 53096 126*53080 53084 53097 126*53080 3072*43000 1024*53020
  //   44160*43000 128*631e0 384*43000 128*631e0 128*43000 128*631e0 3072*43000 128*75100 8064*43000
  //   1024*751c0 3200*43000 128*57000 128*97000 128*d7000 128*43000 128*157000 128*197000 128*1d7000
  //   15360*43000 128*50100 128*50900 128*51100 128*43000 128*50500 128*50d00 15616*43000 128*53100 53105
  //   127*53100 128*5310a 128*5310b 128*53102 53106 31*53100 53107 95*53100 128*53103 128*53104 3072*43000
  //   1024*531a0 11264*43000 128*4a200 128*4aa00 128*4b200 16000*43000 53080 53090 30*53080 53081 95*53080
  //   53085 53093 126*53080 5308a 53091 126*53080 5308b 53092 126*53080 53082 53094 126*53080 53086 53095
  //   30*53080 53087 95*53080 53083 53096 126*53080 53084 53097 126*53080 3072*43000 1024*53020
  //   44160*43000 128*631e0 384*43000 256*631e0 3200*43000 128*75100 8064*43000 1024*751c0 3200*43000
  //   128*57000 128*97000 128*d7000 128*43000 128*157000 128*197000 128*1d7000 15360*43000 128*50100
  //   128*50900 128*51100 128*43000 128*50500 128*50d00 15616*43000 128*53100 53105 127*53100 128*5310a
  //   128*5310b 128*53102 53106 31*53100 53107 95*53100 128*53103 128*53104 3072*43000 1024*531a0
  //   11264*43000 128*4a200 128*4aa00 128*4b200 16000*43000 53080 53090 30*53080 53081 95*53080 53085
  //   53093 126*53080 5308a 53091 126*53080 5308b 53092 126*53080 53082 53094 126*53080 53086 53095
  //   30*53080 53087 95*53080 53083 53096 126*53080 53084 53097 126*53080 3072*43000 1024*53020
  //   44160*43000 128*631e0 256*43000 128*631e0 256*43000 128*631e0 3072*43000 128*75100 8064*43000
  //   1024*751c0 3200*43000 128*57000 128*97000 128*d7000 128*43000 128*157000 128*197000 128*1d7000
  //   15360*43000 128*50100 128*50900 128*51100 128*43000 128*50500 128*50d00 15616*43000 128*53100 53105
  //   127*53100 128*5310a 128*5310b 128*53102 53106 31*53100 53107 95*53100 128*53103 128*53104 3072*43000
  //   1024*531a0 11264*43000 128*4a200 128*4aa00 128*4b200 16000*43000 53080 53090 30*53080 53081 95*53080
  //   53085 53093 126*53080 5308a 53091 126*53080 5308b 53092 126*53080 53082 53094 126*53080 53086 53095
  //   30*53080 53087 95*53080 53083 53096 126*53080 53084 53097 126*53080 3072*43000 1024*53020
  //   44160*43000 128*631e0 256*43000 128*631e0 128*43000 128*631e0 3200*43000 128*75100 8064*43000
  //   1024*751c0 3200*43000 128*57000 128*97000 128*d7000 128*43000 128*157000 128*197000 128*1d7000
  //   15360*43000 128*50100 128*50900 128*51100 128*43000 128*50500 128*50d00 15616*43000 128*53100 53105
  //   127*53100 128*5310a 128*5310b 128*53102 53106 31*53100 53107 95*53100 128*53103 128*53104 3072*43000
  //   1024*531a0 11264*43000 128*4a200 128*4aa00 128*4b200 16000*43000 53080 53090 30*53080 53081 95*53080
  //   53085 53093 126*53080 5308a 53091 126*53080 5308b 53092 126*53080 53082 53094 126*53080 53086 53095
  //   30*53080 53087 95*53080 53083 53096 126*53080 53084 53097 126*53080 3072*43000 1024*53020
  //   44032*43000 128*631e0 512*43000 128*631e0 128*43000 128*631e0 3072*43000 128*75100 8064*43000
  //   1024*751c0 3200*43000 128*57000 128*97000 128*d7000 128*43000 128*157000 128*197000 128*1d7000
  //   15360*43000 128*50100 128*50900 128*51100 128*43000 128*50500 128*50d00 15616*43000 128*53100 53105
  //   127*53100 128*5310a 128*5310b 128*53102 53106 31*53100 53107 95*53100 128*53103 128*53104 3072*43000
  //   1024*531a0 11264*43000 128*4a200 128*4aa00 128*4b200 16000*43000 53080 53090 30*53080 53081 95*53080
  //   53085 53093 126*53080 5308a 53091 126*53080 5308b 53092 126*53080 53082 53094 126*53080 53086 53095
  //   30*53080 53087 95*53080 53083 53096 126*53080 53084 53097 126*53080 3072*43000 1024*53020
  //   44032*43000 128*631e0 512*43000 256*631e0 3200*43000 128*75100 8064*43000 1024*751c0 3200*43000
  //   128*57000 128*97000 128*d700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
endmodule

module Compare (
  input  [31:0] Rs1,
  input  [31:0] Rs2,
  output [2:0] Flags
);

  Comparator #(.width(32)) comparator_1 (.a(Rs1), .b(Rs2), .eq(Flags[2]), .lt(Flags[1]));  // open: gt
  Comparator #(.width(32), .mode("unsigned")) comparator_2 (.a(Rs1), .b(Rs2), .lt(Flags[0]));  // open: gt, eq
endmodule

module Add_4 (
  input  [31:0] Input,
  output [31:0] Output
);

  Adder #(.width(32)) adder_1 (.a(Input), .b(32'h4), .out(Output));  // open: cin, cout
endmodule

module Split_word (
  input  [1:0] Size__Byte_Half_Word,
  input  Signed__Unsigned,
  input  [1:0] Address,
  input  [31:0] Input,
  output Misaligned_split,
  output [31:0] Output
);

  wire or_1_out;
  wire [7:0] multiplexer_1_out;
  wire [15:0] multiplexer_4_out;
  wire [31:0] bit_extender_1_out, bit_extender_2_out, bit_extender_3_out, bit_extender_4_out,
       multiplexer_2_out, multiplexer_6_out;

  assign bit_extender_1_out = {{24{multiplexer_1_out[7]}}, multiplexer_1_out};  // Bit_Extender bit_extender_1
  Multiplexer #(.select(2), .width(8), .enable("false")) multiplexer_1 (
    .in0(Input[7:0]), .in1(Input[15:8]), .in2(Input[23:16]), .in3(Input[31:24]), .out(multiplexer_1_out),
    .sel(Address));
  Multiplexer #(.width(32), .enable("false")) multiplexer_2 (
    .in0(bit_extender_1_out), .in1(bit_extender_2_out), .out(multiplexer_2_out), .sel(Signed__Unsigned));
  assign bit_extender_2_out = {{24{1'b0}}, multiplexer_1_out};  // Bit_Extender bit_extender_2
  Multiplexer #(.select(2), .enable("false")) multiplexer_3 (
    .in0(1'b0), .in1(Address[0]), .in2(or_1_out), .out(Misaligned_split), .sel(Size__Byte_Half_Word));  // open: in3
  assign bit_extender_3_out = {{16{multiplexer_4_out[15]}}, multiplexer_4_out};  // Bit_Extender bit_extender_3
  Multiplexer #(.width(16), .enable("false")) multiplexer_4 (
    .in0(Input[15:0]), .in1(Input[31:16]), .out(multiplexer_4_out), .sel(Address[1]));
  Multiplexer #(.select(2), .width(32), .enable("false")) multiplexer_5 (
    .in0(multiplexer_2_out), .in1(multiplexer_6_out), .in2(Input), .out(Output), .sel(Size__Byte_Half_Word));  // open: in3
  Multiplexer #(.width(32), .enable("false")) multiplexer_6 (
    .in0(bit_extender_3_out), .in1(bit_extender_4_out), .out(multiplexer_6_out), .sel(Signed__Unsigned));
  assign bit_extender_4_out = {{16{1'b0}}, multiplexer_4_out};  // Bit_Extender bit_extender_4
  or or_1 (or_1_out, Address[0], Address[1]);

  // Notes on the sheet:
  //   Byte
  //   Half
  //   Word
endmodule

module Replace_part (
  input  [1:0] Size__Byte_Half_Word,
  input  [31:0] Replacement,
  input  [1:0] Address,
  input  [31:0] Input,
  output Misaligned_Replace,
  output [31:0] Output
);

  wire decoder_1_out0, decoder_1_out1, decoder_1_out2, decoder_1_out3, or_1_out;
  wire [7:0] multiplexer_2_out, multiplexer_3_out, multiplexer_4_out, multiplexer_5_out;
  wire [15:0] multiplexer_6_out, multiplexer_8_out;

  Decoder #(.select(2), .enable("false")) decoder_1 (
    .out0(decoder_1_out0), .out1(decoder_1_out1), .out2(decoder_1_out2), .out3(decoder_1_out3), .sel(Address));
  Multiplexer #(.select(2), .enable("false")) multiplexer_1 (
    .in0(1'b0), .in1(Address[0]), .in2(or_1_out), .out(Misaligned_Replace), .sel(Size__Byte_Half_Word));  // open: in3
  or or_1 (or_1_out, Address[0], Address[1]);
  Multiplexer #(.width(8), .enable("false")) multiplexer_2 (
    .in0(Input[31:24]), .in1(Replacement[7:0]), .out(multiplexer_2_out), .sel(decoder_1_out3));
  Multiplexer #(.width(8), .enable("false")) multiplexer_3 (
    .in0(Input[23:16]), .in1(Replacement[7:0]), .out(multiplexer_3_out), .sel(decoder_1_out2));
  Multiplexer #(.width(8), .enable("false")) multiplexer_4 (
    .in0(Input[15:8]), .in1(Replacement[7:0]), .out(multiplexer_4_out), .sel(decoder_1_out1));
  Multiplexer #(.width(8), .enable("false")) multiplexer_5 (
    .in0(Input[7:0]), .in1(Replacement[7:0]), .out(multiplexer_5_out), .sel(decoder_1_out0));
  Multiplexer #(.width(16), .enable("false")) multiplexer_6 (
    .in0(Input[31:16]), .in1(Replacement[15:0]), .out(multiplexer_6_out), .sel(Address[1]));
  Multiplexer #(.select(2), .width(32), .enable("false")) multiplexer_7 (
    .in0({multiplexer_2_out, multiplexer_3_out, multiplexer_4_out, multiplexer_5_out}),
    .in1({multiplexer_6_out, multiplexer_8_out}), .in2(Replacement), .out(Output), .sel(Size__Byte_Half_Word));  // open: in3
  Multiplexer #(.width(16), .enable("false")) multiplexer_8 (
    .in0(Replacement[15:0]), .in1(Input[15:0]), .out(multiplexer_8_out), .sel(Address[1]));

  // Notes on the sheet:
  //   Byte
  //   Half
  //   Word
endmodule

module CSR (
  input  [4:0] Rs1_uimm,
  input  [4:0] Rd,
  input  [11:0] CSR_specifier,
  input  [31:0] Rs1Val,
  input  [1:0] Operation____RW_RS_RC,
  input  [1:0] DataSrc,
  input  CLK,
  input  CLR,
  input  Imm,
  output Invalid_Read,
  output Invalid_Write,
  output Invalid_Address,
  output Stop_clock,
  output [31:0] Output
);

  wire and_1_out, and_2_out, and_3_out, and_4_out, comparator_1_eq, comparator_2_eq, comparator_3_eq,
       comparator_4_eq, comparator_5_eq, comparator_6_eq, comparator_7_eq, comparator_8_eq, comparator_9_eq,
       comparator_10_eq, comparator_11_eq, comparator_12_eq, counter_1_carry, nand_1_out, nor_1_out,
       nor_2_out, not_1_out, or_1_out, or_2_out, or_3_out, or_4_out;
  wire [31:0] apply_csr_operation_1_newvalue, bit_extender_1_out, controlled_buffer_1_out, counter_1_q,
       counter_2_q, multiplexer_1_out, register_1_q;

  // Probe on and_1_out
  // Probe on and_2_out
  nor nor_1 (nor_1_out, Rs1_uimm[0], Rs1_uimm[1], Rs1_uimm[2], Rs1_uimm[3], Rs1_uimm[4]);
  assign bit_extender_1_out = {{27{1'b0}}, Rs1_uimm};  // Bit_Extender bit_extender_1
  nor nor_2 (nor_2_out, Rd[0], Rd[1], Rd[2], Rd[3], Rd[4]);
  // Probe on CLK
  // Probe on CLR
  and and_1 (and_1_out, or_1_out, and_3_out);
  and and_2 (and_2_out, nand_1_out, and_3_out);
  or or_1 (or_1_out, ~nor_2_out, Operation____RW_RS_RC[1], ~Operation____RW_RS_RC[0]);  // OR_Gate
  nand nand_1 (nand_1_out, nor_1_out, Operation____RW_RS_RC[1]);
  // Probe on apply_csr_operation_1_newvalue
  // Probe on CSR_specifier
  Comparator #(.width(12), .mode("unsigned")) comparator_1 (
    .a(12'h301), .b(CSR_specifier), .eq(comparator_1_eq));  // open: gt, lt
  Comparator #(.width(12), .mode("unsigned")) comparator_2 (
    .a(12'h800), .b(CSR_specifier), .eq(comparator_2_eq));  // open: gt, lt
  Comparator #(.width(12), .mode("unsigned")) comparator_3 (
    .a(12'hc00), .b(CSR_specifier), .eq(comparator_3_eq));  // open: gt, lt
  Comparator #(.width(12), .mode("unsigned")) comparator_4 (
    .a(12'hc01), .b(CSR_specifier), .eq(comparator_4_eq));  // open: gt, lt
  Comparator #(.width(12), .mode("unsigned")) comparator_5 (
    .a(12'hc02), .b(CSR_specifier), .eq(comparator_5_eq));  // open: gt, lt
  Comparator #(.width(12), .mode("unsigned")) comparator_6 (
    .a(12'hc80), .b(CSR_specifier), .eq(comparator_6_eq));  // open: gt, lt
  Comparator #(.width(12), .mode("unsigned")) comparator_7 (
    .a(12'hc80), .b(CSR_specifier), .eq(comparator_7_eq));  // open: gt, lt
  Comparator #(.width(12), .mode("unsigned")) comparator_8 (
    .a(12'hc80), .b(CSR_specifier), .eq(comparator_8_eq));  // open: gt, lt
  Comparator #(.width(12), .mode("unsigned")) comparator_9 (
    .a(12'hf11), .b(CSR_specifier), .eq(comparator_9_eq));  // open: gt, lt
  Comparator #(.width(12), .mode("unsigned")) comparator_10 (
    .a(12'hf12), .b(CSR_specifier), .eq(comparator_10_eq));  // open: gt, lt
  Comparator #(.width(12), .mode("unsigned")) comparator_11 (
    .a(12'hf13), .b(CSR_specifier), .eq(comparator_11_eq));  // open: gt, lt
  Comparator #(.width(12), .mode("unsigned")) comparator_12 (
    .a(12'hf14), .b(CSR_specifier), .eq(comparator_12_eq));  // open: gt, lt
  Comparator #(.width(12), .mode("unsigned")) comparator_13 (
    .a(12'hfc0), .b(CSR_specifier), .eq(Stop_clock));  // open: gt, lt
  and and_3 (and_3_out, DataSrc[1], DataSrc[0]);
  Register #(.width(32), .trigger("falling")) register_1 (
    .D(apply_csr_operation_1_newvalue), .en(and_4_out), .Q(register_1_q), .clk(CLK), .clr(CLR));
  and and_4 (and_4_out, and_2_out, comparator_2_eq);
  or or_2 (or_2_out, comparator_3_eq, comparator_4_eq, comparator_5_eq);
  or or_3 (or_3_out, comparator_6_eq, comparator_7_eq, comparator_8_eq);
  or or_4 (or_4_out, comparator_9_eq, comparator_10_eq, comparator_11_eq, comparator_12_eq);
  assign controlled_buffer_1_out = comparator_2_eq ? register_1_q : 32'bz;  // Controlled_Buffer controlled_buffer_1
  assign controlled_buffer_1_out = or_2_out ? counter_1_q : 32'bz;  // Controlled_Buffer controlled_buffer_2
  Counter #(.width(32), .max('hffffffff)) counter_1 (
    .Q(counter_1_q), .carry(counter_1_carry), .clk(CLK), .clr(CLR));  // open: load, D, count
  assign controlled_buffer_1_out = or_3_out ? counter_2_q : 32'bz;  // Controlled_Buffer controlled_buffer_3
  Counter #(.width(32), .max('hffffffff)) counter_2 (
    .count(counter_1_carry), .Q(counter_2_q), .clk(CLK), .clr(CLR));  // open: load, D, carry
  assign controlled_buffer_1_out = or_4_out ? {32{1'b0}} : 32'bz;  // Controlled_Buffer controlled_buffer_4
  Apply_CSR_operation apply_csr_operation_1 (
    .NewValue(apply_csr_operation_1_newvalue), .PreviousValue(controlled_buffer_1_out),
    .Operation(Operation____RW_RS_RC), .InputValue(multiplexer_1_out));
  Multiplexer #(.width(32), .enable("false")) multiplexer_1 (
    .in0(Rs1Val), .in1(bit_extender_1_out), .out(multiplexer_1_out), .sel(Imm));
  assign controlled_buffer_1_out = comparator_1_eq ? 32'h880001 : 32'bz;  // Controlled_Buffer controlled_buffer_5
  and and_5 (Invalid_Write, and_2_out, or_2_out);
  and and_6 (Invalid_Write, and_2_out, or_3_out);
  assign controlled_buffer_1_out = Stop_clock ? {32{1'b0}} : 32'bz;  // Controlled_Buffer controlled_buffer_6
  and and_7 (Invalid_Read, and_2_out, Stop_clock);
  not not_1 (not_1_out, comparator_1_eq);
  not not_2 (not_1_out, comparator_2_eq);
  not not_3 (not_1_out, or_2_out);
  not not_4 (not_1_out, or_3_out);
  not not_5 (not_1_out, or_4_out);
  not not_6 (not_1_out, Stop_clock);
  Pull_Resistor pull_resistor_1 (.node(Invalid_Read));
  Pull_Resistor pull_resistor_2 (.node(Invalid_Write));
  Pull_Resistor pull_resistor_3 (.node(controlled_buffer_1_out));
  Pull_Resistor #(.pull(1)) pull_resistor_4 (.node(not_1_out));
  and and_8 (Invalid_Address, not_1_out, and_3_out);
  Multiplexer #(.width(32), .enable("false")) multiplexer_2 (
    .in0({32{1'b0}}), .in1(controlled_buffer_1_out), .out(Output), .sel(and_1_out));

  // Notes on the sheet:
  //   SrcZero
  //   DestZero
  //   Read
  //   Write
  //   Using CSR
  //   XLEN: 32
  //   0
  //   Extensions
  //   debug
  //   ureg00
  //   RDCYCLE, RDTIME, RDINSTRET
  //   RDCYCLEH, RDTIMEH, RDINSTRETH
  //   mvenderid, marchid, mimpid, mhartid
  //   misa
  //   and_5 drives only 1 and floats otherwise
  //   and_6 drives only 1 and floats otherwise
  //   and_7 drives only 1 and floats otherwise
  //   not_1 drives only 0 and floats otherwise
  //   not_2 drives only 0 and floats otherwise
  //   not_3 drives only 0 and floats otherwise
  //   not_4 drives only 0 and floats otherwise
  //   not_5 drives only 0 and floats otherwise
  //   not_6 drives only 0 and floats otherwise
endmodule

module Apply_CSR_operation (
  input  [31:0] PreviousValue,
  input  [1:0] Operation,
  input  [31:0] InputValue,
  output [31:0] NewValue
);

  wire [31:0] and_1_out, or_1_out;

  Multiplexer #(.select(2), .width(32), .enable("false")) multiplexer_1 (
    .in1(InputValue), .in2(or_1_out), .in3(and_1_out), .out(NewValue), .sel(Operation));  // open: in0
  assign or_1_out = PreviousValue | InputValue;  // OR_Gate or_1, 32 bits wide
  assign and_1_out = PreviousValue & ~InputValue;  // AND_Gate and_1, 32 bits wide

  // Notes on the sheet:
  //   Write
  //   Set
  //   Clear
endmodule

module I_O (
  input  Keyboard_Available,
  input  [6:0] Keyboard_Data,
  input  [31:0] Data_in,
  input  [31:0] Address,
  input  CLK,
  input  CLR,
  input  Write,
  output CLK_2,
  output Enable_Keyboard,
  output CLR_2,
  output [6:0] TTY_Data,
  output CLK_3,
  output Enable_TTY,
  output CLR_3,
  output [31:0] Screen_1,
  output [31:0] Screen_2,
  output [31:0] Screen_3,
  output [31:0] Screen_4,
  output [31:0] Screen_5,
  output [31:0] Screen_6,
  output [31:0] Screen_7,
  output [31:0] Screen_8,
  output [31:0] Screen_9,
  output [31:0] Screen_10,
  output [31:0] Screen_11,
  output [31:0] Screen_12,
  output [31:0] Screen_13,
  output [31:0] Screen_14,
  output [31:0] Screen_15,
  output [31:0] Screen_16,
  output [31:0] Screen_17,
  output [31:0] Screen_18,
  output [31:0] Screen_19,
  output [31:0] Screen_20,
  output [31:0] Screen_21,
  output [31:0] Screen_22,
  output [31:0] Screen_23,
  output [31:0] Screen_24,
  output [31:0] Screen_25,
  output [31:0] Screen_26,
  output [31:0] Screen_27,
  output [31:0] Screen_28,
  output [31:0] Screen_29,
  output [31:0] Screen_30,
  output [31:0] Screen_31,
  output [31:0] Screen_32,
  output [31:0] Data_out,
  output Valid_Adress
);

  wire and_1_out, comparator_3_eq, decoder_1_out0, decoder_1_out1, decoder_1_out2, decoder_1_out3,
       decoder_1_out4, decoder_1_out5, decoder_1_out6, decoder_1_out7, decoder_1_out8, decoder_1_out9,
       decoder_1_out10, decoder_1_out11, decoder_1_out12, decoder_1_out13, decoder_1_out14, decoder_1_out15,
       decoder_1_out16, decoder_1_out17, decoder_1_out18, decoder_1_out19, decoder_1_out20, decoder_1_out21,
       decoder_1_out22, decoder_1_out23, decoder_1_out24, decoder_1_out25, decoder_1_out26, decoder_1_out27,
       decoder_1_out28, decoder_1_out29, decoder_1_out30, decoder_1_out31;
  wire [31:0] bit_extender_1_out;

  Pull_Resistor pull_resistor_1 (.node(Data_out));
  or or_1 (Valid_Adress, Enable_Keyboard, Enable_TTY, comparator_3_eq);
  Comparator #(.width(32)) comparator_1 (.a(32'hf0000081), .b(Address), .eq(Enable_Keyboard));  // open: gt, lt
  assign bit_extender_1_out = {{25{1'b0}}, Keyboard_Data};  // Bit_Extender bit_extender_1
  assign Data_out = Enable_Keyboard ? bit_extender_1_out : 32'bz;  // Controlled_Buffer controlled_buffer_1
  Comparator #(.width(32)) comparator_2 (.a(32'hf0000080), .b(Address), .eq(Enable_TTY));  // open: gt, lt
  Decoder #(.select(5), .disabled(0)) decoder_1 (
    .out0(decoder_1_out0), .out1(decoder_1_out1), .out2(decoder_1_out2), .out3(decoder_1_out3),
    .out4(decoder_1_out4), .out5(decoder_1_out5), .out6(decoder_1_out6), .out7(decoder_1_out7),
    .out8(decoder_1_out8), .out9(decoder_1_out9), .out10(decoder_1_out10), .out11(decoder_1_out11),
    .out12(decoder_1_out12), .out13(decoder_1_out13), .out14(decoder_1_out14), .out15(decoder_1_out15),
    .out16(decoder_1_out16), .out17(decoder_1_out17), .out18(decoder_1_out18), .out19(decoder_1_out19),
    .out20(decoder_1_out20), .out21(decoder_1_out21), .out22(decoder_1_out22), .out23(decoder_1_out23),
    .out24(decoder_1_out24), .out25(decoder_1_out25), .out26(decoder_1_out26), .out27(decoder_1_out27),
    .out28(decoder_1_out28), .out29(decoder_1_out29), .out30(decoder_1_out30), .out31(decoder_1_out31),
    .sel(Address[6:2]), .en(and_1_out));
  Comparator #(.width(25)) comparator_3 (.a(Address[31:7]), .b(25'h1e00000), .eq(comparator_3_eq));  // open: gt, lt
  Register #(.width(32), .trigger("falling")) register_1 (
    .D(Data_in), .en(decoder_1_out0), .Q(Screen_1), .clk(CLK), .clr(CLR));
  and and_1 (and_1_out, comparator_3_eq, Write);
  Register #(.width(32), .trigger("falling")) register_2 (
    .D(Data_in), .en(decoder_1_out1), .Q(Screen_2), .clk(CLK), .clr(CLR));
  Register #(.width(32), .trigger("falling")) register_3 (
    .D(Data_in), .en(decoder_1_out2), .Q(Screen_3), .clk(CLK), .clr(CLR));
  Register #(.width(32), .trigger("falling")) register_4 (
    .D(Data_in), .en(decoder_1_out3), .Q(Screen_4), .clk(CLK), .clr(CLR));
  Register #(.width(32), .trigger("falling")) register_5 (
    .D(Data_in), .en(decoder_1_out4), .Q(Screen_5), .clk(CLK), .clr(CLR));
  Register #(.width(32), .trigger("falling")) register_6 (
    .D(Data_in), .en(decoder_1_out5), .Q(Screen_6), .clk(CLK), .clr(CLR));
  Register #(.width(32), .trigger("falling")) register_7 (
    .D(Data_in), .en(decoder_1_out6), .Q(Screen_7), .clk(CLK), .clr(CLR));
  Register #(.width(32), .trigger("falling")) register_8 (
    .D(Data_in), .en(decoder_1_out7), .Q(Screen_8), .clk(CLK), .clr(CLR));
  Register #(.width(32), .trigger("falling")) register_9 (
    .D(Data_in), .en(decoder_1_out8), .Q(Screen_9), .clk(CLK), .clr(CLR));
  Register #(.width(32), .trigger("falling")) register_10 (
    .D(Data_in), .en(decoder_1_out9), .Q(Screen_10), .clk(CLK), .clr(CLR));
  Register #(.width(32), .trigger("falling")) register_11 (
    .D(Data_in), .en(decoder_1_out10), .Q(Screen_11), .clk(CLK), .clr(CLR));
  Register #(.width(32), .trigger("falling")) register_12 (
    .D(Data_in), .en(decoder_1_out11), .Q(Screen_12), .clk(CLK), .clr(CLR));
  Register #(.width(32), .trigger("falling")) register_13 (
    .D(Data_in), .en(decoder_1_out12), .Q(Screen_13), .clk(CLK), .clr(CLR));
  Register #(.width(32), .trigger("falling")) register_14 (
    .D(Data_in), .en(decoder_1_out13), .Q(Screen_14), .clk(CLK), .clr(CLR));
  Register #(.width(32), .trigger("falling")) register_15 (
    .D(Data_in), .en(decoder_1_out14), .Q(Screen_15), .clk(CLK), .clr(CLR));
  Register #(.width(32), .trigger("falling")) register_16 (
    .D(Data_in), .en(decoder_1_out15), .Q(Screen_16), .clk(CLK), .clr(CLR));
  Register #(.width(32), .trigger("falling")) register_17 (
    .D(Data_in), .en(decoder_1_out16), .Q(Screen_17), .clk(CLK), .clr(CLR));
  Register #(.width(32), .trigger("falling")) register_18 (
    .D(Data_in), .en(decoder_1_out17), .Q(Screen_18), .clk(CLK), .clr(CLR));
  Register #(.width(32), .trigger("falling")) register_19 (
    .D(Data_in), .en(decoder_1_out18), .Q(Screen_19), .clk(CLK), .clr(CLR));
  Register #(.width(32), .trigger("falling")) register_20 (
    .D(Data_in), .en(decoder_1_out19), .Q(Screen_20), .clk(CLK), .clr(CLR));
  Register #(.width(32), .trigger("falling")) register_21 (
    .D(Data_in), .en(decoder_1_out20), .Q(Screen_21), .clk(CLK), .clr(CLR));
  Register #(.width(32), .trigger("falling")) register_22 (
    .D(Data_in), .en(decoder_1_out21), .Q(Screen_22), .clk(CLK), .clr(CLR));
  Register #(.width(32), .trigger("falling")) register_23 (
    .D(Data_in), .en(decoder_1_out22), .Q(Screen_23), .clk(CLK), .clr(CLR));
  Register #(.width(32), .trigger("falling")) register_24 (
    .D(Data_in), .en(decoder_1_out23), .Q(Screen_24), .clk(CLK), .clr(CLR));
  Register #(.width(32), .trigger("falling")) register_25 (
    .D(Data_in), .en(decoder_1_out24), .Q(Screen_25), .clk(CLK), .clr(CLR));
  Register #(.width(32), .trigger("falling")) register_26 (
    .D(Data_in), .en(decoder_1_out25), .Q(Screen_26), .clk(CLK), .clr(CLR));
  Register #(.width(32), .trigger("falling")) register_27 (
    .D(Data_in), .en(decoder_1_out26), .Q(Screen_27), .clk(CLK), .clr(CLR));
  Register #(.width(32), .trigger("falling")) register_28 (
    .D(Data_in), .en(decoder_1_out27), .Q(Screen_28), .clk(CLK), .clr(CLR));
  Register #(.width(32), .trigger("falling")) register_29 (
    .D(Data_in), .en(decoder_1_out28), .Q(Screen_29), .clk(CLK), .clr(CLR));
  Register #(.width(32), .trigger("falling")) register_30 (
    .D(Data_in), .en(decoder_1_out29), .Q(Screen_30), .clk(CLK), .clr(CLR));
  Register #(.width(32), .trigger("falling")) register_31 (
    .D(Data_in), .en(decoder_1_out30), .Q(Screen_31), .clk(CLK), .clr(CLR));
  Register #(.width(32), .trigger("falling")) register_32 (
    .D(Data_in), .en(decoder_1_out31), .Q(Screen_32), .clk(CLK), .clr(CLR));

  assign CLK_2 = CLK;
  assign CLK_3 = CLK;
  assign CLR_2 = CLR;
  assign CLR_3 = CLR;
  assign TTY_Data = Data_in[6:0];
endmodule

module I_O_test (
);

  wire i_o_1_clk_2, i_o_1_clk_3, i_o_1_clr_2, i_o_1_clr_3, i_o_1_enable_keyboard, i_o_1_enable_tty,
       i_o_2_clk_2, i_o_2_clk_3, i_o_2_clr_2, i_o_2_clr_3, i_o_2_enable_keyboard, i_o_2_enable_tty,
       keyboard_1_avail, keyboard_2_avail;
  wire [6:0] i_o_1_tty_data, i_o_2_tty_data, keyboard_1_data, keyboard_2_data;
  wire [31:0] i_o_1_screen_1, i_o_1_screen_2, i_o_1_screen_3, i_o_1_screen_4, i_o_1_screen_5, i_o_1_screen_6,
       i_o_1_screen_7, i_o_1_screen_8, i_o_1_screen_9, i_o_1_screen_10, i_o_1_screen_11, i_o_1_screen_12,
       i_o_1_screen_13, i_o_1_screen_14, i_o_1_screen_15, i_o_1_screen_16, i_o_1_screen_17, i_o_1_screen_18,
       i_o_1_screen_19, i_o_1_screen_20, i_o_1_screen_21, i_o_1_screen_22, i_o_1_screen_23, i_o_1_screen_24,
       i_o_1_screen_25, i_o_1_screen_26, i_o_1_screen_27, i_o_1_screen_28, i_o_1_screen_29, i_o_1_screen_30,
       i_o_1_screen_31, i_o_1_screen_32, i_o_2_screen_1, i_o_2_screen_2, i_o_2_screen_3, i_o_2_screen_4,
       i_o_2_screen_5, i_o_2_screen_6, i_o_2_screen_7, i_o_2_screen_8, i_o_2_screen_9, i_o_2_screen_10,
       i_o_2_screen_11, i_o_2_screen_12, i_o_2_screen_13, i_o_2_screen_14, i_o_2_screen_15, i_o_2_screen_16,
       i_o_2_screen_17, i_o_2_screen_18, i_o_2_screen_19, i_o_2_screen_20, i_o_2_screen_21, i_o_2_screen_22,
       i_o_2_screen_23, i_o_2_screen_24, i_o_2_screen_25, i_o_2_screen_26, i_o_2_screen_27, i_o_2_screen_28,
       i_o_2_screen_29, i_o_2_screen_30, i_o_2_screen_31, i_o_2_screen_32;

  Keyboard #(.buflen(256)) keyboard_1 (
    .clk(i_o_1_clk_2), .re(i_o_1_clr_2), .clr(i_o_1_enable_keyboard), .avail(keyboard_1_avail),
    .data(keyboard_1_data));
  I_O i_o_1 (
    .CLK_2(i_o_1_clk_2), .CLR_2(i_o_1_clr_2), .Enable_Keyboard(i_o_1_enable_keyboard),
    .Keyboard_Available(keyboard_1_avail), .Keyboard_Data(keyboard_1_data), .CLK_3(i_o_1_clk_3),
    .Enable_TTY(i_o_1_enable_tty), .CLR_3(i_o_1_clr_3), .TTY_Data(i_o_1_tty_data), .Screen_1(i_o_1_screen_1),
    .Screen_2(i_o_1_screen_2), .Screen_3(i_o_1_screen_3), .Screen_4(i_o_1_screen_4),
    .Screen_5(i_o_1_screen_5), .Screen_6(i_o_1_screen_6), .Screen_7(i_o_1_screen_7),
    .Screen_8(i_o_1_screen_8), .Screen_9(i_o_1_screen_9), .Screen_10(i_o_1_screen_10),
    .Screen_11(i_o_1_screen_11), .Screen_12(i_o_1_screen_12), .Screen_13(i_o_1_screen_13),
    .Screen_14(i_o_1_screen_14), .Screen_15(i_o_1_screen_15), .Screen_16(i_o_1_screen_16),
    .Screen_17(i_o_1_screen_17), .Screen_18(i_o_1_screen_18), .Screen_19(i_o_1_screen_19),
    .Screen_20(i_o_1_screen_20), .Screen_21(i_o_1_screen_21), .Screen_22(i_o_1_screen_22),
    .Screen_23(i_o_1_screen_23), .Screen_24(i_o_1_screen_24), .Screen_25(i_o_1_screen_25),
    .Screen_26(i_o_1_screen_26), .Screen_27(i_o_1_screen_27), .Screen_28(i_o_1_screen_28),
    .Screen_29(i_o_1_screen_29), .Screen_30(i_o_1_screen_30), .Screen_31(i_o_1_screen_31),
    .Screen_32(i_o_1_screen_32));  // open: Data_in, Address, Valid_Adress, CLK, CLR, Write, Data_out
  TTY #(.rows(16), .cols(40)) tty_1 (
    .data(i_o_1_tty_data), .clk(i_o_1_clk_3), .we(i_o_1_enable_tty), .clr(i_o_1_clr_3));
  Keyboard #(.buflen(256)) keyboard_2 (
    .clk(i_o_2_clk_2), .re(i_o_2_clr_2), .clr(i_o_2_enable_keyboard), .avail(keyboard_2_avail),
    .data(keyboard_2_data));
  I_O i_o_2 (
    .CLK_2(i_o_2_clk_2), .CLR_2(i_o_2_clr_2), .Enable_Keyboard(i_o_2_enable_keyboard),
    .Keyboard_Available(keyboard_2_avail), .Keyboard_Data(keyboard_2_data), .CLK_3(i_o_2_clk_3),
    .Enable_TTY(i_o_2_enable_tty), .CLR_3(i_o_2_clr_3), .TTY_Data(i_o_2_tty_data), .Screen_1(i_o_2_screen_1),
    .Screen_2(i_o_2_screen_2), .Screen_3(i_o_2_screen_3), .Screen_4(i_o_2_screen_4),
    .Screen_5(i_o_2_screen_5), .Screen_6(i_o_2_screen_6), .Screen_7(i_o_2_screen_7),
    .Screen_8(i_o_2_screen_8), .Screen_9(i_o_2_screen_9), .Screen_10(i_o_2_screen_10),
    .Screen_11(i_o_2_screen_11), .Screen_12(i_o_2_screen_12), .Screen_13(i_o_2_screen_13),
    .Screen_14(i_o_2_screen_14), .Screen_15(i_o_2_screen_15), .Screen_16(i_o_2_screen_16),
    .Screen_17(i_o_2_screen_17), .Screen_18(i_o_2_screen_18), .Screen_19(i_o_2_screen_19),
    .Screen_20(i_o_2_screen_20), .Screen_21(i_o_2_screen_21), .Screen_22(i_o_2_screen_22),
    .Screen_23(i_o_2_screen_23), .Screen_24(i_o_2_screen_24), .Screen_25(i_o_2_screen_25),
    .Screen_26(i_o_2_screen_26), .Screen_27(i_o_2_screen_27), .Screen_28(i_o_2_screen_28),
    .Screen_29(i_o_2_screen_29), .Screen_30(i_o_2_screen_30), .Screen_31(i_o_2_screen_31),
    .Screen_32(i_o_2_screen_32));  // open: Data_in, Address, Valid_Adress, CLK, CLR, Write, Data_out
  DotMatrix #(.inputtype("row"), .matrixcols(32), .matrixrows(32)) dotmatrix_1 (
    .row0(i_o_1_screen_1), .row1(i_o_1_screen_2), .row2(i_o_1_screen_3), .row3(i_o_1_screen_4),
    .row4(i_o_1_screen_5), .row5(i_o_1_screen_6), .row6(i_o_1_screen_7), .row7(i_o_1_screen_8),
    .row8(i_o_1_screen_9), .row9(i_o_1_screen_10), .row10(i_o_1_screen_11), .row11(i_o_1_screen_12),
    .row12(i_o_1_screen_13), .row13(i_o_1_screen_14), .row14(i_o_1_screen_15), .row15(i_o_1_screen_16),
    .row16(i_o_1_screen_17), .row17(i_o_1_screen_18), .row18(i_o_1_screen_19), .row19(i_o_1_screen_20),
    .row20(i_o_1_screen_21), .row21(i_o_1_screen_22), .row22(i_o_1_screen_23), .row23(i_o_1_screen_24),
    .row24(i_o_1_screen_25), .row25(i_o_1_screen_26), .row26(i_o_1_screen_27), .row27(i_o_1_screen_28),
    .row28(i_o_1_screen_29), .row29(i_o_1_screen_30), .row30(i_o_1_screen_31), .row31(i_o_1_screen_32));
  TTY #(.rows(16), .cols(40)) tty_2 (
    .data(i_o_2_tty_data), .clk(i_o_2_clk_3), .we(i_o_2_enable_tty), .clr(i_o_2_clr_3));
  DotMatrix #(.matrixcols(32), .matrixrows(32)) dotmatrix_2 (
    .col0(i_o_2_screen_1), .col1(i_o_2_screen_2), .col2(i_o_2_screen_3), .col3(i_o_2_screen_4),
    .col4(i_o_2_screen_5), .col5(i_o_2_screen_6), .col6(i_o_2_screen_7), .col7(i_o_2_screen_8),
    .col8(i_o_2_screen_9), .col9(i_o_2_screen_10), .col10(i_o_2_screen_11), .col11(i_o_2_screen_12),
    .col12(i_o_2_screen_13), .col13(i_o_2_screen_14), .col14(i_o_2_screen_15), .col15(i_o_2_screen_16),
    .col16(i_o_2_screen_17), .col17(i_o_2_screen_18), .col18(i_o_2_screen_19), .col19(i_o_2_screen_20),
    .col20(i_o_2_screen_21), .col21(i_o_2_screen_22), .col22(i_o_2_screen_23), .col23(i_o_2_screen_24),
    .col24(i_o_2_screen_25), .col25(i_o_2_screen_26), .col26(i_o_2_screen_27), .col27(i_o_2_screen_28),
    .col28(i_o_2_screen_29), .col29(i_o_2_screen_30), .col30(i_o_2_screen_31), .col31(i_o_2_screen_32));
endmodule

module Memory (
  input  I_O_In_Range,
  input  [31:0] I_O_Data,
  input  [31:0] Write_Data,
  input  [31:0] PC,
  input  [31:0] Data_addr,
  input  CLK,
  input  Write,
  input  [1:0] Data_Src,
  input  Signed__Unsigned,
  input  [1:0] Data_size,
  input  CLR_regs,
  output Write_align_exception,
  output Word_aligned_exception,
  output Out_of_range_exception,
  output [31:0] Data,
  output [31:0] Instruction
);

  wire nor_1_out, ram2_1_in_range;
  wire [31:0] ram2_1_data;

  nor nor_1 (nor_1_out, Data_Src[1], Data_Src[0]);
  RAM2 ram2_1 (
    .Write_Data(Write_Data), .PC(PC), .Data_addr(Data_addr), .Data(ram2_1_data), .Instruction(Instruction),
    .Write_align_exception(Write_align_exception), .Word_aligned_exception(Word_aligned_exception),
    .In_Range(ram2_1_in_range), .CLK(CLK), .Write(Write), .Enable(nor_1_out),
    .Signed__Unsigned(Signed__Unsigned), .Data_size(Data_size), .CLR_regs(CLR_regs));
  nor nor_2 (Out_of_range_exception, ram2_1_in_range, I_O_In_Range);
  Multiplexer #(.width(32), .enable("false")) multiplexer_1 (
    .in0(I_O_Data), .in1(ram2_1_data), .out(Data), .sel(ram2_1_in_range));
endmodule

module RAM2 (
  input  [31:0] Write_Data,
  input  [31:0] PC,
  input  [31:0] Data_addr,
  input  CLK,
  input  Write,
  input  Enable,
  input  Signed__Unsigned,
  input  [1:0] Data_size,
  input  CLR_regs,
  output Write_align_exception,
  output Word_aligned_exception,
  output In_Range,
  output [31:0] Data,
  output [31:0] Instruction
);

  wire and_3_out, nor_1_out, not_1_out, replace_part_1_misaligned_replace, split_word_1_misaligned_split;
  wire [31:0] multiplexer_1_out, ram_1_data, replace_part_1_output;

  and and_1 (Write_align_exception, replace_part_1_misaligned_replace, Write);
  Multiplexer #(.width(32), .enable("false")) multiplexer_1 (
    .in0(PC), .in1(Data_addr), .out(multiplexer_1_out), .sel(CLK));
  and and_2 (Word_aligned_exception, split_word_1_misaligned_split, and_3_out);
  Replace_part replace_part_1 (
    .Replacement(Write_Data), .Address(multiplexer_1_out[1:0]), .Size__Byte_Half_Word(Data_size),
    .Misaligned_Replace(replace_part_1_misaligned_replace), .Output(replace_part_1_output), .Input(ram_1_data));
  nor nor_1 (nor_1_out, multiplexer_1_out[26], multiplexer_1_out[27], multiplexer_1_out[28], multiplexer_1_out[29], multiplexer_1_out[30], multiplexer_1_out[31]);
  or or_1 (In_Range, nor_1_out, ~and_3_out);  // OR_Gate
  RAM_part #(.addrWidth(24), .dataWidth(32), .bus("separate")) ram_1 (
    .addr(multiplexer_1_out[25:2]), .din(replace_part_1_output), .data(ram_1_data), .str(Write),
    .sel(nor_1_out), .clk(not_1_out));  // open: ld, clr
  not not_1 (not_1_out, CLK);
  and and_3 (and_3_out, CLK, Enable);
  Split_word split_word_1 (
    .Address(multiplexer_1_out[1:0]), .Size__Byte_Half_Word(Data_size), .Signed__Unsigned(Signed__Unsigned),
    .Misaligned_split(split_word_1_misaligned_split), .Output(Data), .Input(ram_1_data));
  Register #(.width(32)) register_1 (.D(ram_1_data), .Q(Instruction), .clk(CLK), .clr(CLR_regs));  // open: en

  // Notes on the sheet:
  //   Allow Exception
endmodule

module old_main (
  input  CLK,
  input  in_2,
  output [4:0] out_3,
  output [1:0] out_4,
  output [2:0] out_5,
  output out_6,
  output [1:0] out_7,
  output [1:0] out_8,
  output out_9,
  output out_10,
  output out_11,
  output [1:0] out_12,
  output out_13
);

  wire CLR_regs, csr_1_invalid_address, csr_1_invalid_read, csr_1_invalid_write, i_o_1_clk_2, i_o_1_clk_3,
       i_o_1_clr_2, i_o_1_clr_3, i_o_1_enable_keyboard, i_o_1_enable_tty, i_o_1_valid_adress,
       keyboard_1_avail, pc_1_instruction_adress_misaligned_exception, ram_1_out_of_range_exception,
       ram_1_word_aligned_exception, ram_1_write_align_exception;
  wire [2:0] compare_1_flags, split_instruction_1_func3;
  wire [4:0] split_instruction_1_rd, split_instruction_1_rs1, split_instruction_1_rs2;
  wire [6:0] i_o_1_tty_data, keyboard_1_data, split_instruction_1_func7, split_instruction_1_opcode;
  wire [11:0] split_instruction_1_csr_specifier;
  wire [31:0] add_4_1_output, alu_1_result, csr_1_output, i_o_1_data_out, i_o_1_screen_1, i_o_1_screen_2,
       i_o_1_screen_3, i_o_1_screen_4, i_o_1_screen_5, i_o_1_screen_6, i_o_1_screen_7, i_o_1_screen_8,
       i_o_1_screen_9, i_o_1_screen_10, i_o_1_screen_11, i_o_1_screen_12, i_o_1_screen_13, i_o_1_screen_14,
       i_o_1_screen_15, i_o_1_screen_16, i_o_1_screen_17, i_o_1_screen_18, i_o_1_screen_19, i_o_1_screen_20,
       i_o_1_screen_21, i_o_1_screen_22, i_o_1_screen_23, i_o_1_screen_24, i_o_1_screen_25, i_o_1_screen_26,
       i_o_1_screen_27, i_o_1_screen_28, i_o_1_screen_29, i_o_1_screen_30, i_o_1_screen_31, i_o_1_screen_32,
       multiplexer_1_out, multiplexer_2_out, multiplexer_3_out, pc_1_pc, ram_1_data, ram_1_instruction,
       register_file_1_read_data_1, register_file_1_read_data_2, split_instruction_1_imm_b,
       split_instruction_1_imm_i, split_instruction_1_imm_j, split_instruction_1_imm_s,
       split_instruction_1_imm_u, undriven;

  LED led_1 (.in(pc_1_instruction_adress_misaligned_exception));
  PC pc_1 (
    .Jump_Addr(alu_1_result), .PC(pc_1_pc), .Jump(out_11), .CLK(CLK), .RST(CLR_regs),
    .Instruction_adress_misaligned_exception(pc_1_instruction_adress_misaligned_exception));
  Button u_CLR_regs (.out(CLR_regs));
  Keyboard #(.buflen(256)) keyboard_1 (
    .clk(i_o_1_clk_2), .re(i_o_1_clr_2), .clr(i_o_1_enable_keyboard), .avail(keyboard_1_avail),
    .data(keyboard_1_data));
  I_O i_o_1 (
    .CLK_2(i_o_1_clk_2), .CLR_2(i_o_1_clr_2), .Enable_Keyboard(i_o_1_enable_keyboard),
    .Keyboard_Available(keyboard_1_avail), .Keyboard_Data(keyboard_1_data), .CLK_3(i_o_1_clk_3),
    .Enable_TTY(i_o_1_enable_tty), .CLR_3(i_o_1_clr_3), .TTY_Data(i_o_1_tty_data), .Screen_1(i_o_1_screen_1),
    .Screen_2(i_o_1_screen_2), .Screen_3(i_o_1_screen_3), .Screen_4(i_o_1_screen_4),
    .Screen_5(i_o_1_screen_5), .Screen_6(i_o_1_screen_6), .Screen_7(i_o_1_screen_7),
    .Screen_8(i_o_1_screen_8), .Screen_9(i_o_1_screen_9), .Screen_10(i_o_1_screen_10),
    .Screen_11(i_o_1_screen_11), .Screen_12(i_o_1_screen_12), .Screen_13(i_o_1_screen_13),
    .Screen_14(i_o_1_screen_14), .Screen_15(i_o_1_screen_15), .Screen_16(i_o_1_screen_16),
    .Screen_17(i_o_1_screen_17), .Screen_18(i_o_1_screen_18), .Screen_19(i_o_1_screen_19),
    .Screen_20(i_o_1_screen_20), .Screen_21(i_o_1_screen_21), .Screen_22(i_o_1_screen_22),
    .Screen_23(i_o_1_screen_23), .Screen_24(i_o_1_screen_24), .Screen_25(i_o_1_screen_25),
    .Screen_26(i_o_1_screen_26), .Screen_27(i_o_1_screen_27), .Screen_28(i_o_1_screen_28),
    .Screen_29(i_o_1_screen_29), .Screen_30(i_o_1_screen_30), .Screen_31(i_o_1_screen_31),
    .Screen_32(i_o_1_screen_32), .Data_in(undriven), .Valid_Adress(i_o_1_valid_adress), .CLK(CLR_regs),
    .CLR(out_9), .Data_out(i_o_1_data_out));  // open: Address, Write
  LED led_2 (.in(ram_1_write_align_exception));
  LED led_3 (.in(ram_1_out_of_range_exception));
  LED led_4 (.in(ram_1_word_aligned_exception));
  RAM ram_1 (
    .Write_Data(register_file_1_read_data_2), .Data_addr(alu_1_result), .PC(pc_1_pc), .Data(ram_1_data),
    .Instruction(ram_1_instruction), .CLK(CLK), .Write(out_9), .CLR_regs(CLR_regs),
    .Word_aligned_exception(ram_1_word_aligned_exception),
    .Out_of_range_exception(ram_1_out_of_range_exception), .Data_Src(out_8), .Signed__Unsigned(out_6),
    .Data_size(out_7), .Write_align_exception(ram_1_write_align_exception));
  TTY #(.rows(16), .cols(40)) tty_1 (
    .data(i_o_1_tty_data), .clk(i_o_1_clk_3), .we(i_o_1_enable_tty), .clr(i_o_1_clr_3));
  Split_instruction split_instruction_1 (
    .Instruction(ram_1_instruction), .Opcode(split_instruction_1_opcode), .Func3(split_instruction_1_func3),
    .Func7(split_instruction_1_func7), .Rd(split_instruction_1_rd), .Rs1(split_instruction_1_rs1),
    .Rs2(split_instruction_1_rs2), .Imm_I(split_instruction_1_imm_i), .Imm_S(split_instruction_1_imm_s),
    .Imm_B(split_instruction_1_imm_b), .Imm_U(split_instruction_1_imm_u), .Imm_J(split_instruction_1_imm_j),
    .CSR_Specifier(split_instruction_1_csr_specifier));
  Control control_1 (
    .Opcode(split_instruction_1_opcode), .Func3(split_instruction_1_func3),
    .Func7(split_instruction_1_func7), .ALU_op(out_3), .ALU_Src1(out_4), .DataSrc(out_8), .RegWrite(out_10),
    .Jump(out_11), .ALU_Src2(out_5), .Flags(compare_1_flags), .RAMWrite(out_9), .DataSize(out_7),
    .DataSign(out_6), .CSR_Op(out_12), .CSR_Imm(out_13));
  LED led_5 (.in(csr_1_invalid_read));
  Add_4 add_4_1 (.Input(pc_1_pc), .Output(add_4_1_output));
  LED led_6 (.in(csr_1_invalid_address));
  LED led_7 (.in(csr_1_invalid_write));
  CSR csr_1 (
    .Rs1_uimm(split_instruction_1_rs1), .Rd(split_instruction_1_rd),
    .CSR_specifier(split_instruction_1_csr_specifier), .Output(csr_1_output),
    .Rs1Val(register_file_1_read_data_1), .Invalid_Read(csr_1_invalid_read),
    .Invalid_Write(csr_1_invalid_write), .Invalid_Address(csr_1_invalid_address),
    .Operation____RW_RS_RC(out_12), .DataSrc(out_8), .CLK(CLK), .CLR(CLR_regs), .Imm(out_13));  // open: Stop_clock
  DotMatrix #(.inputtype("row"), .matrixcols(32), .matrixrows(32)) dotmatrix_1 (
    .row0(i_o_1_screen_1), .row1(i_o_1_screen_2), .row2(i_o_1_screen_3), .row3(i_o_1_screen_4),
    .row4(i_o_1_screen_5), .row5(i_o_1_screen_6), .row6(i_o_1_screen_7), .row7(i_o_1_screen_8),
    .row8(i_o_1_screen_9), .row9(i_o_1_screen_10), .row10(i_o_1_screen_11), .row11(i_o_1_screen_12),
    .row12(i_o_1_screen_13), .row13(i_o_1_screen_14), .row14(i_o_1_screen_15), .row15(i_o_1_screen_16),
    .row16(i_o_1_screen_17), .row17(i_o_1_screen_18), .row18(i_o_1_screen_19), .row19(i_o_1_screen_20),
    .row20(i_o_1_screen_21), .row21(i_o_1_screen_22), .row22(i_o_1_screen_23), .row23(i_o_1_screen_24),
    .row24(i_o_1_screen_25), .row25(i_o_1_screen_26), .row26(i_o_1_screen_27), .row27(i_o_1_screen_28),
    .row28(i_o_1_screen_29), .row29(i_o_1_screen_30), .row30(i_o_1_screen_31), .row31(i_o_1_screen_32));
  Multiplexer #(.select(2), .width(32), .enable("false")) multiplexer_1 (
    .in0(ram_1_data), .in1(alu_1_result), .in2(add_4_1_output), .in3(csr_1_output), .out(multiplexer_1_out),
    .sel(out_8));
  Compare compare_1 (.Flags(compare_1_flags), .Rs1(register_file_1_read_data_1), .Rs2(register_file_1_read_data_2));
  Register_File register_file_1 (
    .Read_Data_1(register_file_1_read_data_1), .Read_Data_2(register_file_1_read_data_2),
    .Read_Reg_1(split_instruction_1_rs1), .Read_Reg_2(split_instruction_1_rs2),
    .Write_Reg(split_instruction_1_rd), .Write_data(multiplexer_1_out), .RegWrite(out_10), .CLK(CLK),
    .CLR(CLR_regs));
  Multiplexer #(.select(2), .width(32), .enable("false")) multiplexer_2 (
    .in0(register_file_1_read_data_1), .in1(split_instruction_1_imm_u), .in2(split_instruction_1_imm_j),
    .in3(split_instruction_1_imm_b), .out(multiplexer_2_out), .sel(out_4));
  Multiplexer #(.select(3), .width(32), .enable("false")) multiplexer_3 (
    .in0({32{1'b0}}), .in1(register_file_1_read_data_2), .in2(split_instruction_1_imm_i), .in3(pc_1_pc),
    .in4(split_instruction_1_imm_s), .out(multiplexer_3_out), .sel(out_5));  // open: in5, in6, in7
  ALU alu_1 (.Operand1(multiplexer_2_out), .Operand2(multiplexer_3_out), .Operation(out_3), .Result(alu_1_result));

  // Other names for the same wires on the sheet: ALU_op[4:0] = out_3; ALU_Src1[1:0] = out_4; ALU_Src2[2:0] = out_5;
  //   CSR_Imm = out_13; CSR_Op[1:0] = out_12; Data_Sign = out_6; Data_Size[1:0] = out_7; Data_Src[1:0] = out_8;
  //   Jump = out_11; RAMWrite = out_9; RegWrite = out_10

  // Notes on the sheet:
  //   Data-Src: RAM, ALU, PC
  //   ALU-Src1: Reg, Imm-U, Imm-J, Imm-B
  //   ALU-Src2: Zero, Reg, Imm-I, PC, Imm-S
endmodule

module CLK (
  input  Stop_clock,
  input  Manual,
  input  CLR,
  input  Stop,
  input  Start,
  output CLK
);

  wire clock_1_out, or_1_out, s_r_ff_1_q;

  or or_1 (or_1_out, CLR, Stop);
  Multiplexer #(.enable("false")) multiplexer_1 (.in0(clock_1_out), .in1(Manual), .out(CLK), .sel(s_r_ff_1_q));
  S_R_Flip_Flop #(.trigger("falling")) s_r_ff_1 (
    .S(Stop_clock), .clk(CLK), .R(1'b0), .Q(s_r_ff_1_q), .preset(or_1_out), .reset(Start));  // open: Qn, en
  Clock clock_1 (.out(clock_1_out));
endmodule
